# Fritzing sketch AudioPlayer (saved by Fritzing 0.9.4)
breadboards: 1

parts:
  R1 = Resistor [tolerance=±5% resistance=2k package="2512 [SMD]"]
  R7 = Resistor [tolerance=±5% resistance=1k package="2512 [SMD]"]
  R8 = Resistor [tolerance=±5% resistance=1k package="2512 [SMD]"]
  R13 = Resistor [tolerance=±5% resistance=2k package="2512 [SMD]"]
  R14 = Resistor [tolerance=±5% resistance=2k package="2512 [SMD]"]
  R15 = Resistor [tolerance=±5% resistance=2k package="2512 [SMD]"]
  R16 = Resistor [tolerance=±5% resistance=2k package="2512 [SMD]"]
  IC2 = IC, DIP package, 8 pins [chip_label=OPA350]
  Part1 = Arduino Uno (Rev3)
  C1 = Electrolytic Capacitor [capacitance=10μF package="0605 [SMD, electrolytic]"]
  C2 = Electrolytic Capacitor [capacitance=10μF package="0605 [SMD, electrolytic]"]
  Q1 = NPN-Transistor [part_number=PN2222A package="TO92 [THT]"]
  SP1 = SPEAKER [package=pcb_mount_speaker]
  R12 = Resistor [tolerance=±5% resistance=2k package="2512 [SMD]"]
  R6 = Resistor [tolerance=±5% resistance=1k package="2512 [SMD]"]
  R5 = Resistor [tolerance=±5% resistance=1k package="2512 [SMD]"]
  R4 = Resistor [tolerance=±5% resistance=1k package="2512 [SMD]"]
  R11 = Resistor [tolerance=±5% resistance=2k package="2512 [SMD]"]
  R10 = Resistor [tolerance=±5% resistance=2k package="2512 [SMD]"]
  R2 = Resistor [tolerance=±5% resistance=1k package="2512 [SMD]"]
  R9 = Resistor [tolerance=±5% resistance=2k package="2512 [SMD]"]
  R3 = Resistor [tolerance=±5% resistance=1k package="2512 [SMD]"]
  IC1 = IC, DIP package, 8 pins [chip_label=ICL7660]
  U1 = POT [package=alps_pot]

nets (from the schematic view):
  N1: R1.Pin_0, R2.Pin_1, R9.Pin_1
  N2: R1.Pin_1, Part1.GND, C1.+, IC1.pin3, IC1.pin6, U1.E, U1.S
  N3: R7.Pin_0, R8.Pin_1, R15.Pin_1
  N4: R7.Pin_1, R14.Pin_1, R6.Pin_0
  N5: R8.Pin_0, R16.Pin_1, IC2.pin3
  N6: R13.Pin_0, Part1.D6_PWM
  N7: R13.Pin_1, R6.Pin_1, R5.Pin_0
  N8: R14.Pin_0, Part1.D7
  N9: R15.Pin_0, Part1.D8
  N10: R16.Pin_0, Part1.D9_PWM
  N11: IC2.pin2, Q1.E, SP1.-
  N12: IC2.pin4, C1.-, IC1.pin5
  N13: IC2.pin6, Q1.B
  N14: IC2.pin7, Part1.5V, Q1.C, IC1.pin8
  N15: Part1.D2, R9.Pin_0
  N16: Part1.D3_PWM, R10.Pin_0
  N17: Part1.D4, R11.Pin_0
  N18: Part1.D5_PWM, R12.Pin_0
  N19: C2.-, IC1.pin4
  N20: C2.+, IC1.pin2
  N21: SP1.+, U1.A
  N22: R12.Pin_1, R5.Pin_1, R4.Pin_0
  N23: R4.Pin_1, R11.Pin_1, R3.Pin_0
  N24: R10.Pin_1, R2.Pin_0, R3.Pin_1
